# Fritzing sketch PCB (saved by Fritzing 1.0.2b)
circuit board: 10.5cm x 9.7cm

parts:
  R7 = Resistor [tolerance=±5% resistance=1k power=0.25 package=THT]
  R8 = Resistor [tolerance=±5% resistance=180 power=0.25 package=THT]
  R9 = Resistor [tolerance=±5% resistance=1k power=0.25 package=THT]
  555 = 555 Timer [package="DIP8 [THT]"]
  R27 = Resistor [tolerance=±5% resistance=1k power=0.25 package=THT]
  R28 = Resistor [tolerance=±5% resistance=100k power=0.25 package=THT]
  D1 = Rectifier Diode [part_number=1N4001 package="300 mil [THT]"]
  R29 = Resistor [tolerance=±5% power=0.25 resistance=100k package=THT]
  R30 = Resistor [tolerance=±5% power=0.25 resistance=33k package=THT]
  R31 = Resistor [tolerance=±5% resistance=120 power=0.25 package=THT]
  R32 = Resistor [tolerance=±5% resistance=250 power=0.25 package=THT]
  MCP_I = MCP6002 [part_number=_ package="DIP (Dual Inline) [THT]"]
  R37 = Resistor [tolerance=±5% resistance=22k power=0.25 package=THT]
  R38 = Resistor [tolerance=±5% resistance=22k power=0.25 package=THT]
  R39 = Resistor [tolerance=±5% resistance=22k power=0.25 package=THT]
  R40 = Resistor [tolerance=±5% resistance=22k power=0.25 package=THT]
  RELE_2_CANAIS = female pin header, 4 pins [form="♀ (female)"]
  R41 = Resistor [tolerance=±5% power=0.25 resistance=9.1k package=THT]
  R42 = Resistor [tolerance=±5% power=0.25 resistance=1.5k package=THT]
  R43 = Resistor [tolerance=±5% power=0.25 resistance=100k package=THT]
  R44 = Resistor [tolerance=±5% power=0.25 resistance=6.8k package=THT]
  R45 = Resistor [tolerance=±5% power=0.25 resistance=4.7k package=THT]
  MCP_DP = MCP6002 [part_number=_ package="DIP (Dual Inline) [THT]"]
  R51 = Resistor [tolerance=±5% power=0.25 resistance=1.5k package=THT]
  R52 = Resistor [tolerance=±5% power=0.25 resistance=6.8k package=THT]
  R53 = Resistor [tolerance=±5% power=0.25 resistance=9.1k package=THT]
  R55 = Resistor [tolerance=±5% power=0.25 resistance=100k package=THT]
  R57 = Resistor [tolerance=±5% power=0.25 resistance=4.7k package=THT]
  R58 = Resistor [tolerance=±5% power=0.25 resistance=100k package=THT]
  R59 = Resistor [tolerance=±5% power=0.25 resistance=9.1k package=THT]
  R60 = Resistor [tolerance=±5% power=0.25 resistance=1.5k package=THT]
  TL072_I = MCP6002 [part_number=_ package="DIP (Dual Inline) [THT]"]
  J4 = female pin header, 21 pins [form="♀ (female)" part_number=ESP_1]
  J5 = female pin header, 21 pins [form="♀ (female)" part_number=ESP_2]
  R4 = Resistor [tolerance=±5% power=0.25 resistance=5.6k package=THT]
  C11 = Electrolytic Capacitor [capacitance=1µF voltage=35V package="100 mil [THT, electrolytic]"]
  C12 = Electrolytic Capacitor [capacitance=1µF voltage=35V package="100 mil [THT, electrolytic]"]
  C5 = Electrolytic Capacitor [capacitance=1µF voltage=35V package="100 mil [THT, electrolytic]"]
  741 = LM741 [part_number=LM741 package="DIP (Dual Inline) [THT]"]
  A1 = mini560 [package=THT]
  C19 = Electrolytic Capacitor [capacitance=1µF voltage=35V package="100 mil [THT, electrolytic]"]
  C20 = Electrolytic Capacitor [capacitance=1µF voltage=35V package="100 mil [THT, electrolytic]"]
  R61 = Resistor [tolerance=±5% resistance=100k power=0.25 package=THT]
  R62 = Resistor [tolerance=±5% resistance=100k power=0.25 package=THT]
  C17 = Ceramic Capacitor [capacitance=10nF voltage=35V package="200 mil [THT, multilayer]"]
  C21 = Ceramic Capacitor [capacitance=4.7nF voltage=35V package="200 mil [THT, multilayer]"]
  C18 = Ceramic Capacitor [capacitance=10nF voltage=35V package="200 mil [THT, multilayer]"]
  VR2 = TRIMPOT [maximum_resistance=10kΩ knob_status=50% power=0.5W package=3362u-2]
  R63 = Resistor [tolerance=±5% resistance=510 power=0.25 package=THT]
  R64 = Resistor [tolerance=±5% resistance=10k power=0.25 package=THT]
  R65 = Resistor [tolerance=±5% resistance=120 power=0.25 package=THT]
  R66 = Resistor [tolerance=±5% resistance=1k power=0.25 package=THT]
  TL072_DP = MCP6002 [part_number=_ package="DIP (Dual Inline) [THT]"]
  R67 = Resistor [tolerance=±5% resistance=22k power=0.25 package=THT]
  R68 = Resistor [tolerance=±5% resistance=22k power=0.25 package=THT]
  R69 = Resistor [tolerance=±5% resistance=22k power=0.25 package=THT]
  R70 = Resistor [tolerance=±5% resistance=22k power=0.25 package=THT]
  R71 = Resistor [tolerance=±5% resistance=22k power=0.25 package=THT]
  R72 = Resistor [tolerance=±5% resistance=22k power=0.25 package=THT]
  R73 = Resistor [tolerance=±5% resistance=22k power=0.25 package=THT]
  R74 = Resistor [tolerance=±5% resistance=22k power=0.25 package=THT]
  J1 = screw terminal, 2 pins
  J7 = female pin header, 3 pins [form="♀ (female)"]
  ELETRODOS = screw terminal, 2 pins
  ELETRODOS_2 = screw terminal, 2 pins
  J8 = screw terminal, 3 pins
  5V = screw terminal, 2 pins
  ADS115 = Adafruit ADS1115 16Bit I2C ADC [part_number="Adafruit #1085"]
  LM324N = OP482 - Low Power, High Speed JFET Quad Operational Amplifier [part_number=OP482]
  microSD1 = MicroSD Card Module
  M1 = ESP32-S2-DevKitC-1 [part_number=ESP32-S2-DevKitC-1]  # not connected

nets:
  N1: R7.Pin_0, R4.Pin_1, 741.pin2
  N2: R7.Pin_1, VR2.WIPER
  S_R180_1 b: R8.Pin_0, R38.Pin_0, R4.Pin_0, 741.pin6
  S R180 2 b: R8.Pin_1, R37.Pin_0, ELETRODOS.pin1
  N3: R9.Pin_0, 741.pin3
  PWM: R9.Pin_1, J5.pin6
  N4: 555.Trigger, C17.1
  N5: 555.Output, R27.Pin_1
  3.3V: 555.Reset, 555.Vcc_Supply_Voltage, R31.Pin_1, MCP_I.pin8, R44.Pin_1, MCP_DP.pin8, R52.Pin_1, J5.pin21, C20.+, VR2.CW, R64.Pin_1, R66.Pin_1, ADS115.VDD, LM324N.V+
  N6: 555.Control_Voltage, C18.1
  N7: 555.Threshold, R32.Pin_0
  N8: 555.Discharge, R31.Pin_0, R32.Pin_1
  N9: R27.Pin_0, D1.anode, J1.pin2
  GND: R28.Pin_0, R30.Pin_1, MCP_I.pin4, R39.Pin_0, RELE_2_CANAIS.pin1, R43.Pin_1, R45.Pin_0, MCP_DP.pin4, R55.Pin_1, R57.Pin_0, R58.Pin_1, J4.pin21, J5.pin1, C11.-, C12.+, C5.-, A1.pin_3, A1.pin_7, C19.-, C20.-, R62.Pin_0, C17.0, C21.0, C18.0, VR2.CCW, R65.Pin_0, R68.Pin_0, R70.Pin_0, R71.Pin_0, R74.Pin_1, J1.pin1, J7.pin2, ELETRODOS.pin2, J8.pin3, 5V.pin1, ADS115.GND, LM324N.V-, microSD1.GND
  N10: R28.Pin_1, D1.cathode, C5.+, R61.Pin_1
  12V/9V: R29.Pin_0, TL072_I.pin8, C11.+, 741.pin7, A1.pin_1, TL072_DP.pin8, J7.pin1
  BAT: R29.Pin_1, R30.Pin_0, J5.pin8
  S _R180 d u: MCP_I.pin1, R42.Pin_0, R43.Pin_0, ADS115.AIN0
  N11: MCP_I.pin2, R41.Pin_0, R42.Pin_1
  N12: MCP_I.pin3, R44.Pin_0, R45.Pin_1
  N13: R37.Pin_1, R40.Pin_0, TL072_I.pin6
  N14: R38.Pin_1, R39.Pin_1, TL072_I.pin5
  S _R180 d b: R40.Pin_1, R41.Pin_1, TL072_I.pin7
  RL_M: RELE_2_CANAIS.pin2, J5.pin13
  RL_C: RELE_2_CANAIS.pin3, J5.pin12
  5V: RELE_2_CANAIS.pin4, J5.pin2, A1.pin_8, A1.pin_9, C19.+, 5V.pin2, microSD1.VCC
  S_EP_1d u: MCP_DP.pin1, R55.Pin_0, R60.Pin_0, ADS115.AIN1
  N15: MCP_DP.pin2, R59.Pin_0, R60.Pin_1
  N16: MCP_DP.pin3, MCP_DP.pin5, R52.Pin_0, R57.Pin_1
  N17: MCP_DP.pin6, R51.Pin_0, R53.Pin_1
  S_EP_2d u: MCP_DP.pin7, R51.Pin_1, R58.Pin_0, ADS115.AIN2
  S_EP_2d b: R53.Pin_0, TL072_DP.pin7, R67.Pin_1
  S_EP_1d b: R59.Pin_1, TL072_DP.pin1, R73.Pin_0
  -12V: TL072_I.pin4, C12.-, 741.pin4, TL072_DP.pin4, J7.pin3
  SCK: J4.pin1, microSD1.SCK
  MISO: J4.pin2, microSD1.MISO
  S_TEMP: J4.pin3, R63.Pin_1, LM324N.OUTB
  MOSI: J5.pin4, microSD1.MOSI
  CS: J5.pin5, microSD1.CS
  SCL: J5.pin16, ADS115.SCL
  SDA: J5.pin17, ADS115.SDA
  S_MOIST: R61.Pin_0, R62.Pin_1, C21.1, ADS115.AIN3
  N18: R63.Pin_0, R64.Pin_0, R65.Pin_1, LM324N.-INB
  N19: R66.Pin_0, J8.pin1
  N20: TL072_DP.pin2, R73.Pin_1, R74.Pin_0
  N21: TL072_DP.pin3, R71.Pin_1, R72.Pin_0
  N22: TL072_DP.pin5, R68.Pin_1, R69.Pin_1
  N23: TL072_DP.pin6, R67.Pin_0, R70.Pin_1
  S_EP_2 b: R69.Pin_0, ELETRODOS_2.pin1
  S_EP_1 b: R72.Pin_1, ELETRODOS_2.pin2
  N24: J8.pin2, LM324N.+INB

notes:
  I GND
  R CORRENTE
  +12 GND -12
  SMART SOIL SENSOR
  CIRCUITO RELÉS
  CIRCUITO SENSOR UMIDADE SOLO
  CIRCUITO TENSAO BATERIA
  CIRCUITO ADS1015
  CIRCUITO GERADOR SINAL BIPOLAR
  CIRCUITO GERADOR DE SINAL DIFERENCIAL QUEDA R180
  CIRCUITO TRANSFORMADOR DE SINAL BIPOLAR PARA UNIPOLAR
  PARA SINAIS ELETRODOS INTERNOS
  USB
  ANTT
  GND
  5V
  NC
  D11
  D10
  D4
  EN
  VCC
  D5
  D6
  D7
  D15
  RX
  TX
  D41
  D42
  D1
  D2
  D19
  D20
  D8
  D3
  D36
  D0
  D37
  D35
  D16
  D40
  D17
  D39
  D18
  D38
  D46
  D9
  D45
  D48
  D47
  D21
  D14
  D12
  D13
  P2 P1
  pino 1 não é conectado no GND
  CIRCUITO ESP32 S3 NODE MCU
  CIRCUITO REGULADOR DE TENSÃO
  VM
  AZ
  CIRCUITO SENSOR TEMPERATURA DO SOLO
  +12 V
  0 V
  -12 V
  PARA QUEDA R180
  CIRCUITO GERADOR DE SINAL DIFERENCIAL ELETRODOS INTERNOS
  CIRCUITO MODULO MICROSD

custom parts:
  MCP6002: This is a single Op Amp DIP.
  LM741: This is a single Op Amp DIP.
  mini560: 5A DC-DC Mini 560 Step Down Stabilized Voltage Supply Module Output 3.3 5V 9V 12V Step-down Power Converter Board Module
  Adafruit ADS1115 16Bit I2C ADC: For microcontrollers without an analog-to-digital converter or when you want a higher-precision ADC, the ADS1115 provides 16-bit precision at 860 samples/second over I2C. The chip can be configured as 4 single-ended input channels, or two differential channels. As a nice bonus, it even includes a programmable gain amplifier, up to x16, to help boost up smaller single/differential signals to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
  ESP32-S2-DevKitC-1: ESP32-S2-DevKitC-1 is an entry-level development board based on ESP32-S2-SOLO (on-board PCB antenna). It is based on the ESP32 microcontroller that boasts Wifi, Bluetooth, Ethernet and Low Power support all in a single chip. (vanepp) Feb 2022: converted to ESP32-S2-DevKitC-1. This module is 44pins long (2x22) and 11 pins width.
